// Logisim project 5X.circ as structural Verilog
module F (
  input  x1,
  input  x2,
  input  x3,
  input  x4,
  input  x5,
  output F
);

  wire and_1_out, and_2_out, and_3_out, and_4_out, and_5_out, and_6_out, and_7_out, and_8_out, and_9_out,
       and_10_out, and_11_out, and_12_out, not_1_out, not_2_out, not_3_out, not_4_out, not_5_out, not_6_out,
       not_7_out, not_8_out, not_9_out, not_10_out, not_11_out, not_12_out, not_13_out, not_14_out,
       not_15_out, not_16_out, not_17_out, not_18_out, not_19_out, not_20_out, not_21_out, not_22_out,
       not_23_out, not_24_out, not_25_out, not_26_out, not_27_out, not_28_out, not_29_out, not_30_out,
       not_31_out, not_32_out, not_33_out, not_34_out, or_1_out, or_2_out, or_3_out;

  not not_1 (not_1_out, x1);
  not not_2 (not_2_out, x2);
  not not_3 (not_3_out, x2);
  not not_4 (not_4_out, x5);
  not not_5 (not_5_out, x2);
  not not_6 (not_6_out, x2);
  not not_7 (not_7_out, x5);
  not not_8 (not_8_out, x1);
  not not_9 (not_9_out, x2);
  not not_10 (not_10_out, x5);
  not not_11 (not_11_out, x2);
  not not_12 (not_12_out, x5);
  not not_13 (not_13_out, x2);
  not not_14 (not_14_out, x3);
  not not_15 (not_15_out, x5);
  not not_16 (not_16_out, x3);
  not not_17 (not_17_out, x5);
  not not_18 (not_18_out, x1);
  not not_19 (not_19_out, x2);
  not not_20 (not_20_out, x3);
  not not_21 (not_21_out, x2);
  not not_22 (not_22_out, x2);
  not not_23 (not_23_out, x3);
  not not_24 (not_24_out, x2);
  not not_25 (not_25_out, x1);
  not not_26 (not_26_out, x3);
  not not_27 (not_27_out, x2);
  not not_28 (not_28_out, x3);
  not not_29 (not_29_out, x2);
  not not_30 (not_30_out, x1);
  not not_31 (not_31_out, x2);
  not not_32 (not_32_out, x2);
  not not_33 (not_33_out, x2);
  not not_34 (not_34_out, x2);
  and and_1 (and_1_out, not_1_out, not_2_out, x3, not_3_out, not_4_out);
  and and_2 (and_2_out, x1, not_5_out, x3, not_6_out, not_7_out);
  and and_3 (and_3_out, not_8_out, x2, x3, not_9_out, not_10_out);
  and and_4 (and_4_out, x1, x2, x3, not_11_out, not_12_out);
  and and_5 (and_5_out, x1, not_13_out, not_14_out, x2, not_15_out);
  and and_6 (and_6_out, x2, x2, not_16_out, x2, not_17_out);
  and and_7 (and_7_out, not_18_out, not_19_out, not_20_out, not_21_out, x5);
  and and_8 (and_8_out, x1, not_22_out, not_23_out, not_24_out, x5);
  and and_9 (and_9_out, not_25_out, x2, not_26_out, not_27_out, x5);
  and and_10 (and_10_out, x1, x2, not_28_out, not_29_out, x5);
  and and_11 (and_11_out, not_30_out, not_31_out, x3, not_32_out, x5);
  and and_12 (and_12_out, x1, not_33_out, x3, not_34_out, x5);
  or or_1 (or_1_out, and_1_out, and_2_out, and_3_out, and_4_out);
  or or_2 (or_2_out, and_5_out, and_6_out, and_7_out, and_8_out);
  or or_3 (or_3_out, and_9_out, and_10_out, and_11_out, and_12_out);
  or or_4 (F, or_1_out, or_2_out, or_3_out);

  assign x4 = x2;
endmodule
